# Fritzing sketch PDGE4 (saved by Fritzing 0.9.3b)
breadboards: 1

parts:
  part = Arduino Mega 2560 (Rev3)
  RECEPTOR_IR = IR Receiver Breakout [package=PCB]
  LDR_AR = Photocell (LDR) [package=THT]
  LDR_PROJETOR = Photocell (LDR) [package=THT]
  R1 = Resistor [tolerance=±5% resistance=10k package=THT]
  R2 = Resistor [tolerance=±5% resistance=10k package=THT]
  SINAL2 = SWITCH-MOMENTARY-2 [package=tactile-pth-12mm]
  SINAL1 = SWITCH-MOMENTARY-2 [package=tactile-pth-12mm]
  INICIAR = SWITCH-MOMENTARY-2 [package=tactile-pth-12mm]
  R3 = Resistor [tolerance=±5% resistance=1k package=THT]
  R4 = Resistor [tolerance=±5% resistance=1k package=THT]
  R5 = Resistor [tolerance=±5% resistance=1k package=THT]
  LED_FEEDBACK_5mm = LED - 5mm [color="Red (633nm)" package="5 mm [THT]"]
  2N2222 = TRANSISTOR_NPN [package=to-92]
  2N2222_2 = TRANSISTOR_NPN [package=to-92]
  2N2222_3 = TRANSISTOR_NPN [package=to-92]
  R6 = Resistor [tolerance=±5% resistance=470 package=THT]
  R7 = Resistor [tolerance=±5% resistance=470 package=THT]
  R8 = Resistor [tolerance=±5% resistance=470 package=THT]
  LED_IR_5mm = LED - 5mm [color="Infrared (940nm)" package="5 mm [THT]"]
  LED_IR_5mm_2 = LED - 5mm [color="Infrared (940nm)" package="5 mm [THT]"]
  LED_IR_5mm_3 = LED - 5mm [color="Infrared (940nm)" package="5 mm [THT]"]
  SENSOR_PIR = PIR sensor
  2N2222_4 = TRANSISTOR_NPN [package=to-92]
  R9 = Resistor [tolerance=±5% resistance=220 package=THT]
  LED_IR_5mm_4 = LED - 5mm [color="Infrared (940nm)" package="5 mm [THT]"]
  2N2222_5 = TRANSISTOR_NPN [package=to-92]
  R10 = Resistor [tolerance=±5% resistance=220 package=THT]
  LED_IR_5mm_5 = LED - 5mm [color="Infrared (940nm)" package="5 mm [THT]"]
  2N2222_6 = TRANSISTOR_NPN [package=to-92]
  R11 = Resistor [tolerance=±5% resistance=220 package=THT]
  LED_IR_5mm_6 = LED - 5mm [color="Infrared (940nm)" package="5 mm [THT]"]

nets:
  N1: part.A0, LDR_AR.pin_0, R1.Pin_0
  N2: part.A1, LDR_PROJETOR.pin_0, R2.Pin_0
  GND: part.GND, RECEPTOR_IR.GND, LDR_AR.pin_1, LDR_PROJETOR.pin_1, R3.Pin_0, R4.Pin_0, R5.Pin_0, LED_FEEDBACK_5mm.cathode, LED_IR_5mm.cathode, LED_IR_5mm_2.cathode, LED_IR_5mm_3.cathode, SENSOR_PIR.GND, LED_IR_5mm_4.cathode, LED_IR_5mm_5.cathode, LED_IR_5mm_6.cathode
  5V: part.5V, RECEPTOR_IR.VCC, R1.Pin_1, R2.Pin_1, SINAL2.2, SINAL1.2, INICIAR.2, 2N2222.C, 2N2222_2.C, 2N2222_3.C, SENSOR_PIR.VDD, 2N2222_4.C, 2N2222_5.C, 2N2222_6.C
  N3: part.D2_PWM, RECEPTOR_IR.OUT
  N4: part.D5_PWM, SINAL2.1, R3.Pin_1
  N5: part.D6_PWM, SINAL1.1, R4.Pin_1
  N6: part.D7_PWM, INICIAR.1, R5.Pin_1
  N7: part.D37, SENSOR_PIR.SIG
  N8: part.D46, R6.Pin_1, R7.Pin_1, R8.Pin_1, R9.Pin_1
  N9: part.D53, LED_FEEDBACK_5mm.anode
  N10: 2N2222.E, LED_IR_5mm_2.anode
  N11: 2N2222.B, R6.Pin_0
  N12: 2N2222_2.E, LED_IR_5mm_3.anode
  N13: 2N2222_2.B, R7.Pin_0
  N14: 2N2222_3.E, LED_IR_5mm.anode
  N15: 2N2222_3.B, R8.Pin_0
  N16: 2N2222_4.E, LED_IR_5mm_4.anode
  N17: 2N2222_4.B, R9.Pin_0
  N18: 2N2222_5.E, LED_IR_5mm_5.anode
  N19: 2N2222_5.B, R10.Pin_0
  N20: R10.Pin_1, R11.Pin_1
  N21: 2N2222_6.E, LED_IR_5mm_6.anode
  N22: 2N2222_6.B, R11.Pin_0
